# Fritzing sketch air-quality (saved by Fritzing 0.9.6b)
breadboards: 1

parts:
  Bauteil2 = Adafruit CCS811
  U2 = ESP8266 NodeMCU LoLin module

nets:
  3.3V: Bauteil2.3.3V, Bauteil2.!WAKE, U2.3V3
  GND: Bauteil2.GND, U2.GND
  N1: Bauteil2.SDA, U2.D2
  N2: Bauteil2.SCL, U2.D1

custom parts:
  ESP8266 NodeMCU LoLin module: ESP8266 based NodeMCU
